// Logisim project recovered-help.circ as structural Verilog: 1 circuit, main circuit main
module main (
  input  A_b_c,
  input  in_2,
  input  in_3,
  input  in_4,
  output out_5
);

  wire buffer_1_out, not_1_out, not_2_out, This_out;

  // Callout #(.dx(4), .dy(30), .text("Test LabTel")) callout_1: pin names not known; wires that end beside it: in_4
  Multiplexer #(.select(2)) multiplexer_1 ();  // open: in0, in1, in2, in3, out, sel, en
  // Probe on This_out
  not This (This_out, A_b_c);
  not not_1 (not_1_out, in_2);
  not not_2 (not_2_out, in_3);
  // NOT_Gate not_3 is placed but not wired
  buf buffer_1 (buffer_1_out, This_out);
  buf buffer_2 (buffer_1_out, not_1_out);
  buf buffer_3 (buffer_1_out, not_2_out);
  // Buffer buffer_4 has open pins: in=open, out=buffer_1_out
  buf buffer_5 (out_5, buffer_1_out);
  Pull_Resistor #(.pull(1)) pull_resistor_1 (.node(out_5));
  // Callout #(.dx(91), .dy(13), .halign("right"), .text("Second example"), .valign("center")) callout_2: pin names not known

  // Notes on the sheet:
  //   This is an example
  //   This is an example
  //   This is an thirdle
  //   This is an example
  //   This drives only 0 and floats otherwise
  //   not_1 drives only 0 and floats otherwise
  //   not_2 drives only 0 and floats otherwise
  //   not_3 drives only 0 and floats otherwise
endmodule
